// Logisim project Ctl_Load_Store.circ as structural Verilog: 1 circuit, main circuit Load_Store
module Load_Store (
  input  Enable,
  input  Clk,
  input  Reset,
  input  [31:0] Stack_Pointer,
  input  [15:0] Instruction,
  output Store,
  output Load,
  output PC_Hold,
  output [31:0] RAM_Addr,
  output [2:0] Rmd
);

  wire and_3_out, d_ff_1_qn, not_1_out;

  Adder #(.width(32)) adder_1 (
    .a(Stack_Pointer), .b({{24{1'b0}}, Instruction[7:0]}), .out(RAM_Addr));  // open: cin, cout
  and and_1 (Store, Enable, not_1_out);
  not not_1 (not_1_out, Instruction[11]);
  and and_2 (Load, Enable, Instruction[11]);
  and and_3 (and_3_out, Load, d_ff_1_qn);
  D_Flip_Flop d_ff_1 (.D(and_3_out), .clk(Clk), .Q(PC_Hold), .Qn(d_ff_1_qn), .reset(Reset));  // open: preset

  assign Rmd = Instruction[10:8];

  // Notes on the sheet:
  //   Delay load and hold PC for 1 cycle for the RAM to send out requested data 
endmodule
